// Logisim project HW2_RDBL12_S1_NguyenBaoTinh.circ as structural Verilog: 1 circuit, main circuit main
module main (
  input  clk,
  input  rst,
  output [3:0] up
);

  wire and_1_out, D0_qn, D1_qn, D2_qn, D3_qn, or_1_out;

  D_Flip_Flop D0 (.D(D0_qn), .clk(clk), .Q(up[0]), .Qn(D0_qn), .reset(or_1_out));  // open: preset
  or or_1 (or_1_out, rst, and_1_out);
  D_Flip_Flop D1 (.D(D1_qn), .clk(D0_qn), .Q(up[1]), .Qn(D1_qn), .reset(or_1_out));  // open: preset
  D_Flip_Flop D2 (.D(D2_qn), .clk(D1_qn), .Q(up[2]), .Qn(D2_qn), .reset(or_1_out));  // open: preset
  D_Flip_Flop D3 (.D(D3_qn), .clk(D2_qn), .Q(up[3]), .Qn(D3_qn), .reset(or_1_out));  // open: preset
  and and_1 (and_1_out, up[1], up[3]);
endmodule
